// Digital circuit subleq2.dig as structural Verilog
module subleq2 (
  input  [7:0] UI,
  input  in_2,
  input  clk,
  input  in_4
);

  wire acs, and_1_out, and_2_out, and_3_out, comparator_1_eq, comparator_2_eq, comparator_3_eq,
       comparator_4_eq, comparator_5_eq, hex_decode_1_p3, hex_decode_2_p1, hex_decode_2_p4, hex_decode_2_p6,
       hex_decode_3_p3, hex_decode_3_p5, hex_decode_4_p3, hex_decode_4_p5, hex_decode_5_p3, hex_decode_6_p1,
       hex_decode_6_p4, hex_decode_6_p6, inc, jmp, lda, ldb, ldi, ldj, LEQ0, lt, or_1_out, pause, pause_1_p4,
       rdb, rst, wrt;
  wire [3:0] hex_decode_1_p1, hex_decode_1_p4, hex_decode_2_p2, hex_decode_2_p5, hex_decode_3_p1,
       hex_decode_3_p4, hex_decode_4_p1, hex_decode_4_p4, hex_decode_5_p1, hex_decode_5_p4, hex_decode_6_p2,
       hex_decode_6_p5;
  wire [4:0] counter_1_out;
  wire [7:0] alu_1_p4, ARG_2_q, ARG_q, hex_decode_2_p3;
  wire [15:0] ABUS, ADR0_q, PCR_out;

  or or_1 (or_1_out, rst, in_2);
  Seven_Seg_Hex seven_seg_hex_1 (.d(hex_decode_1_p1), .dp(hex_decode_1_p3));
  Register #(.Bits(8)) ARG (.D(alu_1_p4), .C(lt), .en(lda), .Q(ARG_q));
  Counter #(.Bits(5)) counter_1 (.en(1'b1), .C(lt), .clr(or_1_out), .out(counter_1_out));  // open: ovf
  Seven_Seg_Hex seven_seg_hex_2 (.d(hex_decode_1_p4), .dp(hex_decode_2_p1));
  // hex_decode hex_decode_1: pin names not known; wires that end beside it: hex_decode_1_p1, ARG_q, hex_decode_1_p3, hex_decode_1_p4
  Seven_Seg_Hex seven_seg_hex_3 (.d(hex_decode_2_p2), .dp(hex_decode_2_p4));
  Seven_Seg_Hex seven_seg_hex_4 (.d(hex_decode_2_p5), .dp(hex_decode_2_p6));
  // hex_decode hex_decode_2: pin names not known; wires that end beside it: hex_decode_2_p1, hex_decode_2_p2, hex_decode_2_p3, hex_decode_2_p4, hex_decode_2_p5, hex_decode_2_p6
  Register #(.Bits(8)) BRG (.D(alu_1_p4), .C(lt), .en(ldb), .Q(hex_decode_2_p3));
  ROM #(.AddrBits(5), .Bits(10)) ISM (
    .A({LEQ0, counter_1_out[3:0]}), .sel(1'b1), .D({rst, jmp, inc, wrt, ldb, lda, ldj, ldi, rdb, acs}));
  // alu alu_1: pin names not known; wires that end beside it: hex_decode_2_p3, ARG_q, wrt, alu_1_p4, LEQ0
  assign pause = comparator_1_eq ? 1'b1 : 1'bz;  // Driver driver_1
  Seven_Seg_Hex seven_seg_hex_5 (.d(hex_decode_3_p1), .dp(hex_decode_3_p3));
  Seven_Seg_Hex seven_seg_hex_6 (.d(hex_decode_3_p4), .dp(hex_decode_3_p5));
  // hex_decode hex_decode_3: pin names not known; wires that end beside it: hex_decode_3_p1, alu_1_p4, hex_decode_3_p3, hex_decode_3_p4, hex_decode_3_p5
  PullDown #(.Bits(8)) pulldown_1 (.out(alu_1_p4));
  Comparator #(.Bits(16)) comparator_1 (.a({16{1'b1}}), .b(ABUS), .eq(comparator_1_eq));  // open: gt, lt
  RAMSinglePort #(.AddrBits(12), .isProgramMemory("true"), .Bits(8)) MEM (
    .A(ABUS[11:0]), .str(wrt), .C(lt), .ld(and_1_out), .D(alu_1_p4));
  assign alu_1_p4 = and_2_out ? UI : 8'bz;  // Driver driver_2
  and and_1 (and_1_out, comparator_2_eq, rdb);
  and and_2 (and_2_out, comparator_4_eq, rdb);
  Register #(.Bits(8)) ARG_2 (.D(alu_1_p4), .C(lt), .en(and_3_out), .Q(ARG_2_q));
  and and_3 (and_3_out, comparator_3_eq, wrt);
  Comparator #(.Bits(4)) comparator_2 (.a(ABUS[15:12]), .b(4'b0000), .eq(comparator_2_eq));  // open: gt, lt
  Register #(.Bits(8)) ADR1 (.D(alu_1_p4), .C(lt), .en(ldj), .Q(ADR0_q[15:8]));
  Register #(.Bits(8)) ADR0 (.D(alu_1_p4), .C(lt), .en(ldi), .Q(ADR0_q[7:0]));
  Seven_Seg_Hex seven_seg_hex_7 (.d(hex_decode_4_p1), .dp(hex_decode_4_p3));
  Seven_Seg_Hex seven_seg_hex_8 (.d(hex_decode_4_p4), .dp(hex_decode_4_p5));
  // hex_decode hex_decode_4: pin names not known; wires that end beside it: hex_decode_4_p1, ARG_2_q, hex_decode_4_p3, hex_decode_4_p4, hex_decode_4_p5
  Comparator #(.Bits(16)) comparator_3 (.a(16'he001), .b(ABUS), .eq(comparator_3_eq));  // open: gt, lt
  assign ABUS = acs ? ADR0_q : 16'bz;  // Driver driver_3
  Comparator #(.Bits(16)) comparator_4 (.a(16'he000), .b(ABUS), .eq(comparator_4_eq));  // open: gt, lt
  CounterPreset #(.Bits(16)) PCR (
    .en(inc), .C(lt), .dir(1'b0), .in(ADR0_q), .ld(jmp), .clr(in_2), .out(PCR_out));  // open: ovf
  PullDown pulldown_2 (.out(pause));
  // pause pause_1: pin names not known; wires that end beside it: lt, pause, clk, pause_1_p4, in_4
  assign ABUS = ~acs ? PCR_out : 16'bz;  // DriverInvSel driverinvsel_1
  assign pause = comparator_5_eq ? 1'b1 : 1'bz;  // Driver driver_4
  Button button_1 (.out(pause_1_p4));
  Comparator #(.Bits(16)) comparator_5 (.a(16'he000), .b(ABUS), .eq(comparator_5_eq));  // open: gt, lt
  Seven_Seg_Hex seven_seg_hex_9 (.d(hex_decode_5_p1), .dp(hex_decode_5_p3));
  Seven_Seg_Hex seven_seg_hex_10 (.d(hex_decode_5_p4), .dp(hex_decode_6_p1));
  // hex_decode hex_decode_5: pin names not known; wires that end beside it: hex_decode_5_p1, ABUS[15:8], hex_decode_5_p3, hex_decode_5_p4
  Seven_Seg_Hex seven_seg_hex_11 (.d(hex_decode_6_p2), .dp(hex_decode_6_p4));
  Seven_Seg_Hex seven_seg_hex_12 (.d(hex_decode_6_p5), .dp(hex_decode_6_p6));
  // hex_decode hex_decode_6: pin names not known; wires that end beside it: hex_decode_6_p1, hex_decode_6_p2, ABUS[7:0], hex_decode_6_p4, hex_decode_6_p5, hex_decode_6_p6

  // Other names for the same wires on the sheet: ABUSH[3:0] = ABUS[15:12]; reset = in_2

  // Notes on the sheet:
  //   in_2: default 1
  //   clk: Hz: 5
  //   ISM[0x0] = EMEM + LDRG                # load mem[pc] (&A) into ADDR reg
  //   ISM[0x1] = SADR + EMEM + LARG + IPRC  # load mem[&A] into A reg and pc++
  //   ISM[0x2] = EMEM + LDRG                # load mem[pc] (&B) into ADDR reg
  //   ISM[0x3] = SADR + EMEM + LBRG         # load mem[&B] into B addr reg
  //   ISM[0x4] = SDRG + LDOM + IPRC                # load alu out into mem[&B] and pc++
  //   # if leq0=0
  //   ISM[0x5] = IPRC + RISC                # pc++ and reset inctruction counter
  //   # if leq0=1
  //   ISM[0xd] = EMEM + LPRC + RISC         # load mem[pc] (&C) into pc and reset inctruction counter
  //   ISM[0x8] = ISM[0x0]
  //   ISM[0x9] = ISM[0x1]
  //   ISM[0xa] = ISM[0x2]
  //   ISM[0xb] = ISM[0x3]
  //   ISM[0xc] = ISM[0x4]
  //   contents of ISM (hex, n*v repeats v):
  //   86,a,93,86,a,23,c1,80,280,7*0,86,a,93,86,a,23,c1,86,a,300
  //   Halt
  //   Pause for user
endmodule
